// Logisim project ALU.circ as structural Verilog: 1 circuit, main circuit ALU
module ALU (
  input  [31:0] Operador_A,
  input  [31:0] Operador_B,
  input  [3:0] Op_selector,
  input  [1:0] Sel_Hi,
  output [31:0] out_5,
  output out_6,
  output out_7,
  output [31:0] out_8
);

  wire comparator_2_eq;
  wire [0:0] con_signo, con_signo_t, con_signo_t_t, con_signo_t_t_t, sin_signo, sin_signo_t, sin_signo_t_t,
       sin_signo_t_t_t, tunnel_t_t;
  wire [31:0] And, Hi__Div, Hi__Divu, Hi__Mul, Hi__Mulu, Lo__Div, Lo__Divu, Lo__Mul, Lo__Mulu, Nor, Or,
       tunnel, tunnel_t, undriven, undriven_2, undriven_3, Xor;

  // Probe on Operador_A
  // Probe on Operador_B
  // Probe on Op_selector
  Multiplexer #(.select(2), .width(32), .enable("false")) multiplexer_1 (
    .in0(Hi__Mul), .in1(Hi__Mulu), .in2(Hi__Div), .in3(Hi__Divu), .out(out_8), .sel(Sel_Hi));
  // Probe on tunnel
  Adder #(.width(32)) adder_1 (.a(Operador_A), .b(Operador_B), .out(tunnel));  // open: cin, cout
  Subtractor #(.width(32)) subtractor_1 (.a(Operador_A), .b(Operador_B), .out(tunnel_t));  // open: bin, bout
  Multiplier #(.width(32)) multiplier_1 (.a(Operador_A), .b(Operador_B), .out(Lo__Mulu), .cout(Hi__Mulu));  // open: cin
  Div div_1 (.A(Operador_A), .B(Operador_B), .Hi(Hi__Mul), .Lo(Lo__Mul));
  Divider #(.width(32)) divider_1 (.a(Operador_A), .b(Operador_B), .out(Lo__Divu), .rem(Hi__Divu));  // open: upper
  Div div_2 (.A(Operador_A), .B(Operador_B), .Hi(Hi__Div), .Lo(Lo__Div));
  assign And = Operador_A & Operador_B;  // AND_Gate and_1, 32 bits wide
  assign Or = Operador_A | Operador_B;  // OR_Gate or_1, 32 bits wide
  assign Nor = ~(Operador_A | Operador_B);  // NOR_Gate nor_1, 32 bits wide
  assign Xor = Operador_A ^ Operador_B;  // XOR_Gate xor_1, 32 bits wide
  Comparator #(.width(32)) comparator_1 (
    .a(Operador_A), .b(Operador_B), .gt(con_signo_t_t[0]), .eq(tunnel_t_t[0]), .lt(con_signo[0]));
  Comparator #(.width(32), .mode("unsigned")) comparator_2 (
    .a(Operador_A), .b(Operador_B), .gt(sin_signo_t_t[0]), .eq(comparator_2_eq), .lt(sin_signo[0]));
  or or_2 (con_signo_t_t_t[0], con_signo_t_t[0], tunnel_t_t[0]);
  or or_3 (con_signo_t[0], tunnel_t_t[0], con_signo[0]);
  or or_4 (sin_signo_t_t_t[0], sin_signo_t_t[0], comparator_2_eq);
  or or_5 (sin_signo_t[0], comparator_2_eq, sin_signo[0]);
  Comparator #(.width(32)) comparator_3 (.a(out_5), .b({32{1'b0}}), .eq(out_6), .lt(out_7));  // open: gt
  // Probe on out_5
  // Probe on out_8
  Multiplexer #(.select(4), .width(32)) multiplexer_2 (
    .in0(tunnel), .in1(tunnel_t), .in2(Lo__Mul), .in3(Lo__Div), .in4(Lo__Mulu), .in5(Lo__Divu), .in6(And),
    .in7(Or), .in8(Nor), .in9(Xor), .in10({{31{1'b0}}, con_signo[0]}), .in11({{31{1'b0}}, sin_signo[0]}),
    .in12(Operador_A), .in13(undriven), .in14(undriven_2), .in15(undriven_3), .out(out_5), .sel(Op_selector));  // open: en
  // Probe on out_5

  // Other names for the same wires on the sheet: A[31:0] = Operador_A; B[31:0] = Operador_B; Hi[31:0] = out_8;
  //   N_flag = out_7; OP[3:0] = Op_selector; Salida[31:0] = out_5; Z_flag = out_6

  // Notes on the sheet:
  //   Slt
  //   Sltu
endmodule
