// Logisim project Mult Y Div Sin signo.circ as structural Verilog: 2 circuits, main circuit Div
module Div (
  input  [31:0] A,
  input  [31:0] B,
  output [31:0] Hi,
  output [31:0] Lo
);

  wire [31:0] multiplexer_1_out, multiplexer_2_out, negator_1_out, negator_2_out;

  // Probe on A
  // Probe on B
  Negator #(.width(32)) negator_1 (.in(A), .out(negator_1_out));
  Negator #(.width(32)) negator_2 (.in(B), .out(negator_2_out));
  Multiplexer #(.width(32)) multiplexer_1 (
    .in0(A), .in1(negator_1_out), .out(multiplexer_1_out), .sel(A[31]));  // open: en
  Multiplexer #(.width(32)) multiplexer_2 (
    .in0(B), .in1(negator_2_out), .out(multiplexer_2_out), .sel(B[31]));  // open: en
  // Probe on multiplexer_1_out
  Divider #(.width(32)) divider_1 (.a(multiplexer_1_out), .b(multiplexer_2_out), .out(Lo), .rem(Hi));  // open: upper
  // Probe on multiplexer_2_out
  // Probe on Hi
  // Probe on Lo

  // Other names for the same wires on the sheet: Sign_A = A[31]; Sign_B = B[31]
endmodule

module mult (
  input  [31:0] A,
  input  [31:0] B
);

  wire [31:0] Hi, Lo, multiplexer_1_out, multiplexer_2_out, negator_1_out, negator_2_out;

  // Probe on A
  // Probe on B
  Negator #(.width(32)) negator_1 (.in(A), .out(negator_1_out));
  // Probe on negator_1_out
  Negator #(.width(32)) negator_2 (.in(B), .out(negator_2_out));
  // Probe on negator_2_out
  Multiplexer #(.width(32), .enable("false")) multiplexer_1 (
    .in0(B), .in1(negator_2_out), .out(multiplexer_1_out), .sel(B[31]));
  // Probe on multiplexer_2_out
  Multiplexer #(.width(32), .enable("false")) multiplexer_2 (
    .in0(A), .in1(negator_1_out), .out(multiplexer_2_out), .sel(A[31]));
  // Probe on multiplexer_1_out
  Multiplier #(.width(32)) multiplier_1 (
    .a(multiplexer_2_out), .b(multiplexer_1_out), .out(Lo), .cout(Hi));  // open: cin

  // Other names for the same wires on the sheet: Sign_A = A[31]; Sign_B = B[31]

  // Notes on the sheet:
  //   Multiplicador sin signo
endmodule
